# Fritzing sketch sketch (saved by Fritzing 0.9.3b)
breadboards: 1

parts:
  Raspberry_Pi_1 = Raspberry Pi 3 [part_number=RPI-3-V1.2]
  LED_1 = LED - 5mm [color="Blue (470nm)" package="5 mm [THT]"]
  R3 = Resistor [tolerance=±5% resistance=100 package=THT]

nets:
  N1: Raspberry_Pi_1.GND, R3.Pin_0
  N2: LED_1.cathode, R3.Pin_1

notes:
  LED 1 (Phy pin 7)
