# Fritzing sketch sketch_analog (saved by Fritzing 0.9.3b)
breadboards: 1

parts:
  Raspberry_Pi_1 = Raspberry Pi 3 [part_number=RPI-3-V1.2]
  Composant1 = Soil Moisture Sensor
  Composant2 = Soil Moisture Sensor
  Composant3 = Soil Moisture Sensor
  Q1 = NPN-Transistor [package="TO92 [THT]"]
  R1 = Resistor [tolerance=±5% resistance=1.5k package=THT]
  Composant4 = ADS1115

nets:
  N1: Raspberry_Pi_1.GPIO2, Composant4.SDA
  N2: Raspberry_Pi_1.GPIO3, Composant4.SCL
  GND: Raspberry_Pi_1.GND, Q1.E, Composant4.GND, Composant4.ADDR
  N3: Raspberry_Pi_1.GPIO18, R1.Pin_0
  VCC: Raspberry_Pi_1.5V, Composant1.VCC, Composant2.VCC, Composant3.VCC, Composant4.VDD
  GND_2: Composant1.GND, Composant2.GND, Composant3.GND, Q1.C
  N4: Composant1.SIG, Composant4.A2
  N5: Composant2.SIG, Composant4.A1
  N6: Composant3.SIG, Composant4.A0
  N7: Q1.B, R1.Pin_1

custom parts:
  ADS1115: ADC ADS1115
