# Fritzing sketch sketch_digital (saved by Fritzing 0.9.3b)
breadboards: 1

parts:
  Raspberry_Pi_1 = Raspberry Pi 3 [part_number=RPI-3-V1.2]
  Composant1 = Soil Moisture Sensor
  Composant2 = Soil Moisture Sensor
  Composant3 = Soil Moisture Sensor
  Q1 = NPN-Transistor [package="TO92 [THT]"]
  R1 = Resistor [tolerance=±5% resistance=1.5k package=THT]

nets:
  N1: Raspberry_Pi_1.GPIO17, Composant1.SIG
  N2: Raspberry_Pi_1.GPIO27, Composant2.SIG
  N3: Raspberry_Pi_1.GPIO22, Composant3.SIG
  N4: Raspberry_Pi_1.GPIO18, R1.Pin_0
  N5: Raspberry_Pi_1.GND, Q1.E
  VCC: Raspberry_Pi_1.5V, Composant1.VCC, Composant2.VCC, Composant3.VCC
  GND: Composant1.GND, Composant2.GND, Composant3.GND, Q1.C
  N6: Q1.B, R1.Pin_1
