# Fritzing sketch sketch_pump (saved by Fritzing 0.9.3b)
breadboards: 1

parts:
  Raspberry_Pi_1 = Raspberry Pi 3 [part_number=RPI-3-V1.2]
  M1 = DC Motor
  R1 = Resistor [tolerance=±5% resistance=220 package="0402 [SMD]"]
  U1 = DIODE-ZENER [package=diode-zener]
  Q1 = TRANSISTOR_NPN [package=to-92-ammo]
  R2 = Resistor [tolerance=±5% resistance=1.5k package=THT]
  Q2 = pnp-Powertransistor [package="TO220 [THT]"]
  R3 = Resistor [tolerance=±5% resistance=10k package="1206 [SMD]"]

nets:
  N1: Raspberry_Pi_1.GPIO4, R2.Pin_0
  N2: Raspberry_Pi_1.GND, M1.pin_1, R1.Pin_1, U1.A, Q1.C
  N3: M1.pin_2, U1.C, Q2.collector
  N4: R1.Pin_0, Q2.emitter, R3.Pin_1
  N5: Q1.E, Q2.base, R3.Pin_0
  N6: Q1.B, R2.Pin_1

notes:
  Power 12V DC
  Pump 12V DC
